// Logisim project LambdaCalculus.circ as structural Verilog
module main (
  input  CLK
);

  wire [21:0] Bus1In, Bus1Out;

  Selector selector_1 (
    .IN1(Bus1Out), .OUT1(Bus1In), .SelfBusInput(Bus1In), .SelfBusOutput(Bus1Out), .CLK(CLK),
    .UniqueNodeID(4'b0001), .IN1_2(Bus1Out), .OUT1_2(Bus1In));  // open: IN2, OUT2, IN3, OUT3, IN4, OUT4, IN5, OUT5, IN6, OUT6, IN7, OUT7, IN8, OUT8, IN9, OUT9, IN10, OUT10, IN11, OUT11, IN12, OUT12, IN13, OUT13, IN14, OUT14, IN15, OUT15, IN2_2, OUT2_2, IN3_2, OUT3_2, IN4_2, OUT4_2, IN5_2, OUT5_2, IN6_2, OUT6_2, IN7_2, OUT7_2, IN8_2, OUT8_2, IN9_2, OUT9_2, IN10_2, OUT10_2, IN11_2, OUT11_2, IN12_2, OUT12_2, IN13_2, OUT13_2, IN14_2, OUT14_2, IN15_2, OUT15_2

  // Notes on the sheet:
  //   4,4
  //   Resolve Flag: [Flag State]
  //   [1-bit]
  //   Expression Data: [Resolve Flag, Expression Type, Child Left, Child right]
  //   1,3,4,4
  //   Instruction Data: [Instruction, Address Contents]
  //   [8-bit]
  //   Reduce Flag: [Flag State]
  //   [1-bit]
  //   [12-bit]
  //   22-bit bus
  //   Expression Type
  //   Undefined: 000
  //   Name: 001
  //   Application: 010
  //   Function: 011
  //   Goto: 100
  //   [Expression, Instruction, Resolve, Reduce]
endmodule

module Selector (
  input  [21:0] SelfBusInput,
  input  [21:0] IN1,
  input  CLK,
  input  [21:0] IN1_2,
  input  [3:0] UniqueNodeID,
  input  [21:0] IN2,
  input  [21:0] IN2_2,
  input  [21:0] IN3,
  input  [21:0] IN3_2,
  input  [21:0] IN4,
  input  [21:0] IN4_2,
  input  [21:0] IN5,
  input  [21:0] IN5_2,
  input  [21:0] IN6,
  input  [21:0] IN6_2,
  input  [21:0] IN7,
  input  [21:0] IN7_2,
  input  [21:0] IN8,
  input  [21:0] IN8_2,
  input  [21:0] IN9,
  input  [21:0] IN9_2,
  input  [21:0] IN10,
  input  [21:0] IN10_2,
  input  [21:0] IN11,
  input  [21:0] IN11_2,
  input  [21:0] IN12,
  input  [21:0] IN12_2,
  input  [21:0] IN13,
  input  [21:0] IN13_2,
  input  [21:0] IN14,
  input  [21:0] IN14_2,
  input  [21:0] IN15,
  input  [21:0] IN15_2,
  output [21:0] SelfBusOutput,
  output [21:0] OUT1,
  output [21:0] OUT1_2,
  output [21:0] OUT2,
  output [21:0] OUT2_2,
  output [21:0] OUT3,
  output [21:0] OUT3_2,
  output [21:0] OUT4,
  output [21:0] OUT4_2,
  output [21:0] OUT5,
  output [21:0] OUT5_2,
  output [21:0] OUT6,
  output [21:0] OUT6_2,
  output [21:0] OUT7,
  output [21:0] OUT7_2,
  output [21:0] OUT8,
  output [21:0] OUT8_2,
  output [21:0] OUT9,
  output [21:0] OUT9_2,
  output [21:0] OUT10,
  output [21:0] OUT10_2,
  output [21:0] OUT11,
  output [21:0] OUT11_2,
  output [21:0] OUT12,
  output [21:0] OUT12_2,
  output [21:0] OUT13,
  output [21:0] OUT13_2,
  output [21:0] OUT14,
  output [21:0] OUT14_2,
  output [21:0] OUT15,
  output [21:0] OUT15_2
);

  wire decoder_1_out0, decoder_1_out1, decoder_1_out2, decoder_1_out3, decoder_1_out4, decoder_1_out5,
       decoder_1_out6, decoder_1_out7, decoder_1_out8, decoder_1_out9, decoder_1_out10, decoder_1_out11,
       decoder_1_out12, decoder_1_out13, decoder_1_out14, decoder_1_out15, decoder_2_out0, decoder_2_out1,
       decoder_2_out2, decoder_2_out3, decoder_2_out4, decoder_2_out5, decoder_2_out6, decoder_2_out7,
       decoder_2_out8, decoder_2_out9, decoder_2_out10, decoder_2_out11, decoder_2_out12, decoder_2_out13,
       decoder_2_out14, decoder_2_out15;
  wire [3:0] node_1_p1, node_1_p8;
  wire [21:0] controlled_buffer_1_out, node_1_p3, node_1_p9, node_1_p10;

  assign controlled_buffer_1_out = decoder_1_out1 ? IN1 : 22'bz;  // Controlled_Buffer controlled_buffer_1
  assign OUT1 = decoder_1_out1 ? node_1_p3 : 22'bz;  // Controlled_Buffer controlled_buffer_2
  assign controlled_buffer_1_out = decoder_1_out2 ? IN2 : 22'bz;  // Controlled_Buffer controlled_buffer_3
  assign OUT2 = decoder_1_out2 ? node_1_p3 : 22'bz;  // Controlled_Buffer controlled_buffer_4
  assign controlled_buffer_1_out = decoder_1_out3 ? IN3 : 22'bz;  // Controlled_Buffer controlled_buffer_5
  assign OUT3 = decoder_1_out3 ? node_1_p3 : 22'bz;  // Controlled_Buffer controlled_buffer_6
  assign controlled_buffer_1_out = decoder_1_out4 ? IN4 : 22'bz;  // Controlled_Buffer controlled_buffer_7
  assign OUT4 = decoder_1_out4 ? node_1_p3 : 22'bz;  // Controlled_Buffer controlled_buffer_8
  Decoder #(.select(4)) decoder_1 (
    .out0(decoder_1_out0), .out1(decoder_1_out1), .out2(decoder_1_out2), .out3(decoder_1_out3),
    .out4(decoder_1_out4), .out5(decoder_1_out5), .out6(decoder_1_out6), .out7(decoder_1_out7),
    .out8(decoder_1_out8), .out9(decoder_1_out9), .out10(decoder_1_out10), .out11(decoder_1_out11),
    .out12(decoder_1_out12), .out13(decoder_1_out13), .out14(decoder_1_out14), .out15(decoder_1_out15),
    .sel(node_1_p1));  // open: en
  assign controlled_buffer_1_out = decoder_1_out5 ? IN5 : 22'bz;  // Controlled_Buffer controlled_buffer_9
  assign OUT5 = decoder_1_out5 ? node_1_p3 : 22'bz;  // Controlled_Buffer controlled_buffer_10
  assign controlled_buffer_1_out = decoder_1_out6 ? IN6 : 22'bz;  // Controlled_Buffer controlled_buffer_11
  assign OUT6 = decoder_1_out6 ? node_1_p3 : 22'bz;  // Controlled_Buffer controlled_buffer_12
  assign controlled_buffer_1_out = decoder_1_out7 ? IN7 : 22'bz;  // Controlled_Buffer controlled_buffer_13
  assign OUT7 = decoder_1_out7 ? node_1_p3 : 22'bz;  // Controlled_Buffer controlled_buffer_14
  assign controlled_buffer_1_out = decoder_1_out8 ? IN8 : 22'bz;  // Controlled_Buffer controlled_buffer_15
  assign OUT8 = decoder_1_out8 ? node_1_p3 : 22'bz;  // Controlled_Buffer controlled_buffer_16
  assign controlled_buffer_1_out = decoder_1_out9 ? IN9 : 22'bz;  // Controlled_Buffer controlled_buffer_17
  assign OUT9 = decoder_1_out9 ? node_1_p3 : 22'bz;  // Controlled_Buffer controlled_buffer_18
  assign controlled_buffer_1_out = decoder_1_out10 ? IN10 : 22'bz;  // Controlled_Buffer controlled_buffer_19
  assign OUT10 = decoder_1_out10 ? node_1_p3 : 22'bz;  // Controlled_Buffer controlled_buffer_20
  assign controlled_buffer_1_out = decoder_1_out11 ? IN11 : 22'bz;  // Controlled_Buffer controlled_buffer_21
  assign OUT11 = decoder_1_out11 ? node_1_p3 : 22'bz;  // Controlled_Buffer controlled_buffer_22
  assign controlled_buffer_1_out = decoder_1_out12 ? IN12 : 22'bz;  // Controlled_Buffer controlled_buffer_23
  assign OUT12 = decoder_1_out12 ? node_1_p3 : 22'bz;  // Controlled_Buffer controlled_buffer_24
  assign controlled_buffer_1_out = decoder_1_out13 ? IN13 : 22'bz;  // Controlled_Buffer controlled_buffer_25
  assign OUT13 = decoder_1_out13 ? node_1_p3 : 22'bz;  // Controlled_Buffer controlled_buffer_26
  assign controlled_buffer_1_out = decoder_1_out14 ? IN14 : 22'bz;  // Controlled_Buffer controlled_buffer_27
  assign OUT14 = decoder_1_out14 ? node_1_p3 : 22'bz;  // Controlled_Buffer controlled_buffer_28
  assign controlled_buffer_1_out = decoder_1_out15 ? IN15 : 22'bz;  // Controlled_Buffer controlled_buffer_29
  assign OUT15 = decoder_1_out15 ? node_1_p3 : 22'bz;  // Controlled_Buffer controlled_buffer_30
  // Node node_1: pin names not known; wires that end beside it: node_1_p1, controlled_buffer_1_out, node_1_p3, SelfBusInput, CLK, SelfBusOutput, UniqueNodeID, node_1_p8, node_1_p9, node_1_p10
  assign node_1_p9 = decoder_2_out1 ? IN14_2 : 22'bz;  // Controlled_Buffer controlled_buffer_31
  assign OUT14_2 = decoder_2_out1 ? node_1_p10 : 22'bz;  // Controlled_Buffer controlled_buffer_32
  assign node_1_p9 = decoder_2_out0 ? IN15_2 : 22'bz;  // Controlled_Buffer controlled_buffer_33
  assign OUT15_2 = decoder_2_out0 ? node_1_p10 : 22'bz;  // Controlled_Buffer controlled_buffer_34
  assign node_1_p9 = decoder_2_out3 ? IN12_2 : 22'bz;  // Controlled_Buffer controlled_buffer_35
  assign OUT12_2 = decoder_2_out3 ? node_1_p10 : 22'bz;  // Controlled_Buffer controlled_buffer_36
  assign node_1_p9 = decoder_2_out2 ? IN13_2 : 22'bz;  // Controlled_Buffer controlled_buffer_37
  assign OUT13_2 = decoder_2_out2 ? node_1_p10 : 22'bz;  // Controlled_Buffer controlled_buffer_38
  assign node_1_p9 = decoder_2_out5 ? IN10_2 : 22'bz;  // Controlled_Buffer controlled_buffer_39
  assign OUT10_2 = decoder_2_out5 ? node_1_p10 : 22'bz;  // Controlled_Buffer controlled_buffer_40
  assign node_1_p9 = decoder_2_out4 ? IN11_2 : 22'bz;  // Controlled_Buffer controlled_buffer_41
  assign OUT11_2 = decoder_2_out4 ? node_1_p10 : 22'bz;  // Controlled_Buffer controlled_buffer_42
  Decoder #(.select(4)) decoder_2 (
    .out0(decoder_2_out0), .out1(decoder_2_out1), .out2(decoder_2_out2), .out3(decoder_2_out3),
    .out4(decoder_2_out4), .out5(decoder_2_out5), .out6(decoder_2_out6), .out7(decoder_2_out7),
    .out8(decoder_2_out8), .out9(decoder_2_out9), .out10(decoder_2_out10), .out11(decoder_2_out11),
    .out12(decoder_2_out12), .out13(decoder_2_out13), .out14(decoder_2_out14), .out15(decoder_2_out15),
    .sel(node_1_p8));  // open: en
  assign node_1_p9 = decoder_2_out7 ? IN8_2 : 22'bz;  // Controlled_Buffer controlled_buffer_43
  assign OUT8_2 = decoder_2_out7 ? node_1_p10 : 22'bz;  // Controlled_Buffer controlled_buffer_44
  assign node_1_p9 = decoder_2_out6 ? IN9_2 : 22'bz;  // Controlled_Buffer controlled_buffer_45
  assign OUT9_2 = decoder_2_out6 ? node_1_p10 : 22'bz;  // Controlled_Buffer controlled_buffer_46
  assign node_1_p9 = decoder_2_out9 ? IN6_2 : 22'bz;  // Controlled_Buffer controlled_buffer_47
  assign OUT6_2 = decoder_2_out9 ? node_1_p10 : 22'bz;  // Controlled_Buffer controlled_buffer_48
  assign node_1_p9 = decoder_2_out8 ? IN7_2 : 22'bz;  // Controlled_Buffer controlled_buffer_49
  assign OUT7_2 = decoder_2_out8 ? node_1_p10 : 22'bz;  // Controlled_Buffer controlled_buffer_50
  assign node_1_p9 = decoder_2_out11 ? IN4_2 : 22'bz;  // Controlled_Buffer controlled_buffer_51
  assign OUT4_2 = decoder_2_out11 ? node_1_p10 : 22'bz;  // Controlled_Buffer controlled_buffer_52
  assign node_1_p9 = decoder_2_out10 ? IN5_2 : 22'bz;  // Controlled_Buffer controlled_buffer_53
  assign OUT5_2 = decoder_2_out10 ? node_1_p10 : 22'bz;  // Controlled_Buffer controlled_buffer_54
  assign node_1_p9 = decoder_2_out13 ? IN2_2 : 22'bz;  // Controlled_Buffer controlled_buffer_55
  assign OUT2_2 = decoder_2_out13 ? node_1_p10 : 22'bz;  // Controlled_Buffer controlled_buffer_56
  assign node_1_p9 = decoder_2_out12 ? IN3_2 : 22'bz;  // Controlled_Buffer controlled_buffer_57
  assign OUT3_2 = decoder_2_out12 ? node_1_p10 : 22'bz;  // Controlled_Buffer controlled_buffer_58
  assign node_1_p9 = decoder_2_out14 ? IN1_2 : 22'bz;  // Controlled_Buffer controlled_buffer_59
  assign OUT1_2 = decoder_2_out14 ? node_1_p10 : 22'bz;  // Controlled_Buffer controlled_buffer_60
endmodule

module Node (
  input  NewNodeReturn,
  input  [21:0] ParentIn,
  input  [3:0] NewID,
  input  [21:0] ChildLeftIn,
  input  [21:0] ChildRightIn,
  input  Clock,
  input  [3:0] UniqueNodeID,
  output NewNodeRequest,
  output [21:0] ParentOut,
  output [21:0] ChildLeftOut,
  output [21:0] ChildRightOut,
  output [3:0] ChildLeftPointerOut,
  output [3:0] ChildRightPointerOut
);

  wire and_1_out, and_2_out, d_ff_1_q, d_ff_2_q, nameexpression_1_p8, nameexpression_1_p10,
       nameexpression_1_p12, nameexpression_1_p14, nameexpression_1_p15, nameexpression_1_p16,
       nameexpression_1_p17, nameexpression_5_p12, or_1_out, or_2_out, or_3_out;
  wire [2:0] ExpressionBuffer, nameexpression_1_p27, not_1_out, not_2_out, xor_1_out, xor_2_out;
  wire [3:0] controlled_buffer_1_out, nameexpression_1_p19, NewNode, register_4_q, register_6_q;
  wire [7:3] nameexpression_1_p27_2;
  wire [11:0] nameexpression_1_p26;

  assign not_1_out = ~xor_1_out;  // NOT_Gate not_1, 3 bits wide
  assign xor_1_out = ChildLeftIn[10:8] ^ 3'b011;  // XOR_Gate xor_1, 3 bits wide
  Register #(.width(4)) register_1 (
    .D(nameexpression_1_p26[3:0]), .en(nameexpression_1_p8), .clk(Clock), .Q(ChildLeftIn[15:12]));  // open: clr
  Register #(.width(4)) register_2 (
    .D(nameexpression_1_p26[7:4]), .en(nameexpression_1_p8), .clk(Clock), .Q(ChildLeftIn[19:16]));  // open: clr
  Register #(.width(3)) register_3 (
    .D(nameexpression_1_p26[10:8]), .en(nameexpression_1_p8), .clk(Clock), .Q(ChildLeftIn[10:8]));  // open: clr
  assign xor_2_out = ChildLeftIn[10:8] ^ 3'b001;  // XOR_Gate xor_2, 3 bits wide
  assign not_2_out = ~xor_2_out;  // NOT_Gate not_2, 3 bits wide
  and and_1 (and_1_out, not_1_out[0], not_1_out[1], not_1_out[2]);
  D_Flip_Flop d_ff_1 (.D(or_1_out), .clk(Clock), .Q(d_ff_1_q), .reset(nameexpression_1_p15));  // open: Qn, preset
  and and_2 (and_2_out, not_2_out[0], not_2_out[1], not_2_out[2]);
  or or_1 (or_1_out, and_2_out, or_2_out);
  and and_3 (ChildLeftIn[11], d_ff_1_q, or_2_out);
  or or_2 (or_2_out, ChildLeftIn[20], ChildRightIn[20]);
  or or_3 (or_3_out, and_1_out, ParentIn[21]);
  D_Flip_Flop d_ff_2 (.D(ParentIn[21]), .clk(Clock), .Q(d_ff_2_q));  // open: Qn, preset, reset
  // NameExpression nameexpression_1: pin names not known; wires that end beside it: {ChildLeftIn[11:8], ChildLeftIn[19:12]}, {ChildLeftIn[11:8], ChildLeftIn[19:12]}, {ChildLeftIn[11:8], ChildLeftIn[19:12]}, {ChildLeftIn[11:8], ChildLeftIn[19:12]}, {ChildLeftIn[11:8], ChildLeftIn[19:12]}, {ChildLeftIn[11:8], ChildLeftIn[19:12]}, {ChildLeftIn[11:8], ChildLeftIn[19:12]}, nameexpression_1_p8, ExpressionBuffer, nameexpression_1_p10, Clock, nameexpression_1_p12, UniqueNodeID, nameexpression_1_p14, nameexpression_1_p15, nameexpression_1_p16, nameexpression_1_p17, NewNodeRequest, nameexpression_1_p19, ParentOut[11:0], ParentOut[19:12], ChildRightOut[11:0], ChildRightOut[19:12], ChildLeftOut[11:0], ChildLeftOut[19:12], nameexpression_1_p26, {nameexpression_1_p27_2, nameexpression_1_p27}
  or or_4 (ChildRightOut[21], or_3_out, d_ff_2_q);
  // NameExpression nameexpression_2: pin names not known; wires that end beside it: {ChildLeftIn[11:8], ChildLeftIn[19:12]}, {ChildLeftIn[11:8], ChildLeftIn[19:12]}, {ChildLeftIn[11:8], ChildLeftIn[19:12]}, {ChildLeftIn[11:8], ChildLeftIn[19:12]}, {ChildLeftIn[11:8], ChildLeftIn[19:12]}, {ChildLeftIn[11:8], ChildLeftIn[19:12]}, {ChildLeftIn[11:8], ChildLeftIn[19:12]}, nameexpression_1_p14, ExpressionBuffer, nameexpression_1_p10, Clock, nameexpression_1_p12, UniqueNodeID, nameexpression_1_p14, nameexpression_1_p15, nameexpression_1_p16, nameexpression_1_p17, NewNodeRequest, nameexpression_1_p19, nameexpression_1_p26, {nameexpression_1_p27_2, nameexpression_1_p27}, ChildRightOut[11:0], ChildRightOut[19:12], ChildLeftOut[11:0], ChildLeftOut[19:12], ParentOut[11:0], ParentOut[19:12]
  // NameExpression nameexpression_3: pin names not known; wires that end beside it: {ChildLeftIn[11:8], ChildLeftIn[19:12]}, {ChildLeftIn[11:8], ChildLeftIn[19:12]}, {ChildLeftIn[11:8], ChildLeftIn[19:12]}, {ChildLeftIn[11:8], ChildLeftIn[19:12]}, {ChildLeftIn[11:8], ChildLeftIn[19:12]}, {ChildLeftIn[11:8], ChildLeftIn[19:12]}, {ChildLeftIn[11:8], ChildLeftIn[19:12]}, nameexpression_1_p14, ExpressionBuffer, nameexpression_1_p10, Clock, nameexpression_1_p12, UniqueNodeID, nameexpression_1_p14, nameexpression_1_p15, nameexpression_1_p16, nameexpression_1_p17, NewNodeRequest, nameexpression_1_p19, ParentOut[11:0], ParentOut[19:12], ChildRightOut[11:0], ChildRightOut[19:12], ChildLeftOut[11:0], ChildLeftOut[19:12], nameexpression_1_p26, {nameexpression_1_p27_2, nameexpression_1_p27}
  // NameExpression nameexpression_4: pin names not known; wires that end beside it: {ChildLeftIn[11:8], ChildLeftIn[19:12]}, {ChildLeftIn[11:8], ChildLeftIn[19:12]}, {ChildLeftIn[11:8], ChildLeftIn[19:12]}, {ChildLeftIn[11:8], ChildLeftIn[19:12]}, {ChildLeftIn[11:8], ChildLeftIn[19:12]}, {ChildLeftIn[11:8], ChildLeftIn[19:12]}, {ChildLeftIn[11:8], ChildLeftIn[19:12]}, nameexpression_1_p14, ExpressionBuffer, nameexpression_1_p10, Clock, nameexpression_1_p12, UniqueNodeID, nameexpression_1_p14, nameexpression_1_p15, nameexpression_1_p16, nameexpression_1_p17, NewNodeRequest, nameexpression_1_p19, ParentOut[11:0], ParentOut[19:12], ChildRightOut[11:0], ChildRightOut[19:12], ChildLeftOut[11:0], ChildLeftOut[19:12], nameexpression_1_p26, {nameexpression_1_p27_2, nameexpression_1_p27}
  // NameExpression nameexpression_5: pin names not known; wires that end beside it: {ChildLeftIn[11:8], ChildLeftIn[19:12]}, {ChildLeftIn[11:8], ChildLeftIn[19:12]}, {ChildLeftIn[11:8], ChildLeftIn[19:12]}, {ChildLeftIn[11:8], ChildLeftIn[19:12]}, {ChildLeftIn[11:8], ChildLeftIn[19:12]}, {ChildLeftIn[11:8], ChildLeftIn[19:12]}, {ChildLeftIn[11:8], ChildLeftIn[19:12]}, nameexpression_1_p14, ExpressionBuffer, nameexpression_1_p10, Clock, nameexpression_5_p12, UniqueNodeID, nameexpression_1_p14, nameexpression_1_p15, nameexpression_1_p16, nameexpression_1_p17, NewNodeRequest, nameexpression_1_p19, ParentOut[11:0], ParentOut[19:12], ChildRightOut[11:0], ChildRightOut[19:12], ChildLeftOut[11:0], ChildLeftOut[19:12], nameexpression_1_p26, {nameexpression_1_p27_2, nameexpression_1_p27}
  Register #(.width(4)) register_4 (
    .D({nameexpression_1_p27_2[3], nameexpression_1_p27}), .en(nameexpression_1_p12), .clk(Clock),
    .Q(register_4_q), .clr(nameexpression_1_p17));
  Register #(.width(4)) NewNodeID (.D(NewID), .en(NewNodeRequest), .clk(NewNodeReturn), .Q(NewNode));  // open: clr
  assign controlled_buffer_1_out = nameexpression_1_p12 ? register_4_q : 4'bz;  // Controlled_Buffer controlled_buffer_1
  RAM #(.addrWidth(4), .dataWidth(4), .databus("bibus")) ram_1 (
    .addr(controlled_buffer_1_out), .we(nameexpression_1_p16), .oe(1'b1), .clk(Clock), .din(NewNode),
    .dout(nameexpression_1_p19));
  Register #(.width(3)) register_5 (
    .D(nameexpression_1_p27), .en(nameexpression_1_p10), .clk(Clock), .Q(ExpressionBuffer));  // open: clr
  Register #(.width(4)) register_6 (
    .D({nameexpression_1_p27_2[3], nameexpression_1_p27}), .en(nameexpression_1_p14), .clk(Clock),
    .Q(register_6_q), .clr(nameexpression_1_p17));
  assign controlled_buffer_1_out = nameexpression_1_p14 ? register_6_q : 4'bz;  // Controlled_Buffer controlled_buffer_2
  // Pins of 4 and 8 bits meet at {nameexpression_1_p27_2, nameexpression_1_p27}
  // Pins of 8 and 12 bits meet at {ChildLeftIn[11:8], ChildLeftIn[19:12]}

  assign ChildLeftIn[7:0] = ChildLeftIn[19:12];
  assign ChildLeftOut[21:20] = 2'b00;
  assign ChildLeftPointerOut = ChildLeftIn[19:16];
  assign ChildRightIn[19:0] = {ChildLeftIn[19:8], ChildLeftIn[19:12]};
  assign ChildRightOut[20] = 1'b0;
  assign ChildRightPointerOut = ChildLeftIn[15:12];
  assign ParentIn[19:0] = {ChildLeftIn[19:8], ChildLeftIn[19:12]};
  assign ParentOut[21:20] = {ChildRightOut[21], ChildLeftIn[11]};

  // Other names for the same wires on the sheet: Expression[2:0] = ChildLeftIn[10:8];
  //   ChildRight[3:0] = ChildLeftIn[15:12]; ChildLeft[3:0] = ChildLeftIn[19:16]

  // Notes on the sheet:
  //   Resolve Flag
  //   Reduce Flag
  //   FrontStack
  //   BackStack
endmodule

module UndefinedExpression (
  input  [11:0] PEB,
  input  [7:0] PIB,
  input  [11:0] CRE,
  input  [7:0] CRI,
  input  [11:0] CLE,
  input  [7:0] CLI,
  input  [11:0] InternalExpression,
  output [11:0] PEB_2,
  output [7:0] PIB_2,
  output [11:0] CRE_2,
  output [7:0] CRI_2,
  output [11:0] CLE_2,
  output [7:0] CLI_2
);

  wire decoder_1_out0;

  Decoder #(.select(4)) decoder_1 (
    .out0(decoder_1_out0), .sel(PIB[7:4]));  // open: out1, out2, out3, out4, out5, out6, out7, out8, out9, out10, out11, out12, out13, out14, out15, en
  assign PEB_2 = decoder_1_out0 ? {12{1'b0}} : 12'bz;  // Controlled_Buffer controlled_buffer_1
  assign PIB_2 = decoder_1_out0 ? {8{1'b0}} : 8'bz;  // Controlled_Buffer controlled_buffer_2
  assign CRE_2 = decoder_1_out0 ? {12{1'b0}} : 12'bz;  // Controlled_Buffer controlled_buffer_3
  assign CRI_2 = decoder_1_out0 ? {8{1'b0}} : 8'bz;  // Controlled_Buffer controlled_buffer_4
  assign CLE_2 = decoder_1_out0 ? {12{1'b0}} : 12'bz;  // Controlled_Buffer controlled_buffer_5
  assign CLI_2 = decoder_1_out0 ? {8{1'b0}} : 8'bz;  // Controlled_Buffer controlled_buffer_6

  // Notes on the sheet:
  //   Input
  //   Output
endmodule

module NameExpression (
  input  [11:0] PEB,
  input  [7:0] PIB,
  input  [11:0] CRE,
  input  [7:0] CRI,
  input  [11:0] CLE,
  input  [7:0] CLI,
  input  [7:0] in_7,
  input  [11:0] InternalExpression,
  input  Clock,
  input  [2:0] ExpressionBuffer,
  input  [3:0] UniqueNodeID,
  output EXPWrite,
  output EXBWrite,
  output FrontStack,
  output BackStack,
  output RAMwrite,
  output NewNode,
  output [11:0] PEB_2,
  output [7:0] PIB_2,
  output [11:0] CRE_2,
  output [7:0] CRI_2,
  output [11:0] CLE_2,
  output [7:0] CLI_2,
  output [11:0] NewNode_2,
  output [7:0] GeneralOutput,
  output EXPWrite_2,
  output StackClear
);

  wire decoder_1_out1, decoder_1_out2, decoder_1_out3, decoder_1_out4, decoder_1_out5, not_1_out, not_2_out,
       not_3_out, not_4_out, not_5_out, not_6_out, not_7_out, not_8_out, nullification_1_nullcli,
       nullification_1_nullcri, nullification_1_nullexp, nullification_1_nullstackclear, or_1_out, or_2_out,
       or_3_out, or_4_out, or_6_out, or_7_out, or_8_out, or_9_out, or_11_out, or_12_out, or_13_out,
       or_14_out, or_15_out, or_16_out, or_17_out, or_18_out, or_19_out, or_20_out,
       returnexpression_1_retcli, returnexpression_1_retcri, returnexpression_1_retpeb,
       returnexpression_1_retpib, updateexpression_1_updcli, updateexpression_1_updcri,
       updateexpression_1_updexp, updateexpression_1_updstackclear, updatepointerleft_1_updcli,
       updatepointerleft_1_updcri, updatepointerleft_1_updexp, updatepointerright_1_updcli,
       updatepointerright_1_updcri, updatepointerright_1_updexp;
  wire [7:0] nullification_1_cli, nullification_1_cri, returnexpression_1_cli_2, returnexpression_1_cri_2,
       returnexpression_1_pib_2, updateexpression_1_cli, updateexpression_1_cri, updatepointerleft_1_cli,
       updatepointerleft_1_cri, updatepointerright_1_cli, updatepointerright_1_cri;
  wire [11:0] nullification_1_newvalue, returnexpression_1_peb, updateexpression_1_newvalue,
       updatepointerleft_1_newvalue, updatepointerright_1_newvalue;

  Decoder #(.select(4)) decoder_1 (
    .out1(decoder_1_out1), .out2(decoder_1_out2), .out3(decoder_1_out3), .out4(decoder_1_out4),
    .out5(decoder_1_out5), .sel(PIB[7:4]));  // open: out0, out6, out7, out8, out9, out10, out11, out12, out13, out14, out15, en
  Nullification nullification_1 (
    .ActivationSignal(decoder_1_out1), .Clock(Clock), .NullCLI(nullification_1_nullcli),
    .NullCRI(nullification_1_nullcri), .NullStackClear(nullification_1_nullstackclear),
    .NullEXP(nullification_1_nullexp), .CRI(nullification_1_cri), .CLI(nullification_1_cli),
    .NewValue(nullification_1_newvalue));
  assign CRI_2 = nullification_1_nullcli ? nullification_1_cri : 8'bz;  // Controlled_Buffer controlled_buffer_1
  assign CLI_2 = nullification_1_nullcri ? nullification_1_cli : 8'bz;  // Controlled_Buffer controlled_buffer_2
  assign NewNode_2 = nullification_1_nullexp ? nullification_1_newvalue : 12'bz;  // Controlled_Buffer controlled_buffer_3
  or or_1 (or_1_out, nullification_1_nullexp, updateexpression_1_updexp);
  or or_2 (or_2_out, nullification_1_nullcli, updateexpression_1_updcri);
  assign CRI_2 = updateexpression_1_updcri ? updateexpression_1_cri : 8'bz;  // Controlled_Buffer controlled_buffer_4
  UpdateExpression updateexpression_1 (
    .ActivationSignal(decoder_1_out2), .Clock(Clock), .UniqueNodeID(UniqueNodeID), .PIB(PIB), .PEB(PEB),
    .UpdCLI(updateexpression_1_updcli), .UpdCRI(updateexpression_1_updcri),
    .UpdStackClear(updateexpression_1_updstackclear), .UpdEXP(updateexpression_1_updexp),
    .CRI(updateexpression_1_cri), .CLI(updateexpression_1_cli), .NewValue(updateexpression_1_newvalue));
  or or_3 (or_3_out, nullification_1_nullcri, updateexpression_1_updcli);
  assign CLI_2 = updateexpression_1_updcli ? updateexpression_1_cli : 8'bz;  // Controlled_Buffer controlled_buffer_5
  or or_4 (or_4_out, nullification_1_nullexp, updateexpression_1_updexp);
  assign NewNode_2 = updateexpression_1_updexp ? updateexpression_1_newvalue : 12'bz;  // Controlled_Buffer controlled_buffer_6
  or or_5 (StackClear, nullification_1_nullstackclear, updateexpression_1_updstackclear);
  or or_6 (or_6_out, or_1_out, updatepointerleft_1_updexp);
  or or_7 (or_7_out, or_2_out, updatepointerleft_1_updcri);
  assign CRI_2 = updatepointerleft_1_updcri ? updatepointerleft_1_cri : 8'bz;  // Controlled_Buffer controlled_buffer_7
  or or_8 (or_8_out, or_3_out, updatepointerleft_1_updcli);
  assign CLI_2 = updatepointerleft_1_updcli ? updatepointerleft_1_cli : 8'bz;  // Controlled_Buffer controlled_buffer_8
  or or_9 (or_9_out, or_4_out, updatepointerleft_1_updexp);
  assign NewNode_2 = updatepointerleft_1_updexp ? updatepointerleft_1_newvalue : 12'bz;  // Controlled_Buffer controlled_buffer_9
  UpdatePointerLeft updatepointerleft_1 (
    .ActivationSignal(decoder_1_out3), .Clock(Clock), .UniqueNodeID(UniqueNodeID), .PIB(PIB),
    .InternalExpression(InternalExpression), .PEB(PEB), .UpdCLI(updatepointerleft_1_updcli),
    .UpdCRI(updatepointerleft_1_updcri), .UpdEXP(updatepointerleft_1_updexp), .CRI(updatepointerleft_1_cri),
    .CLI(updatepointerleft_1_cli), .NewValue(updatepointerleft_1_newvalue));
  UpdatePointerRight updatepointerright_1 (
    .ActivationSignal(decoder_1_out4), .Clock(Clock), .UniqueNodeID(UniqueNodeID), .PIB(PIB),
    .InternalExpression(InternalExpression), .PEB(PEB), .UpdCLI(updatepointerright_1_updcli),
    .UpdCRI(updatepointerright_1_updcri), .UpdEXP(updatepointerright_1_updexp),
    .CRI(updatepointerright_1_cri), .CLI(updatepointerright_1_cli), .NewValue(updatepointerright_1_newvalue));
  or or_10 (EXPWrite, or_6_out, updatepointerright_1_updexp);
  or or_11 (or_11_out, or_7_out, updatepointerright_1_updcri);
  assign CRI_2 = updatepointerright_1_updcri ? updatepointerright_1_cri : 8'bz;  // Controlled_Buffer controlled_buffer_10
  or or_12 (or_12_out, or_8_out, updatepointerright_1_updcli);
  assign CLI_2 = updatepointerright_1_updcli ? updatepointerright_1_cli : 8'bz;  // Controlled_Buffer controlled_buffer_11
  or or_13 (or_13_out, or_9_out, updatepointerright_1_updexp);
  assign NewNode_2 = updatepointerright_1_updexp ? updatepointerright_1_newvalue : 12'bz;  // Controlled_Buffer controlled_buffer_12
  ReturnExpression returnexpression_1 (
    .ActivationSignal(decoder_1_out5), .UniqueNodeID(UniqueNodeID), .PIB(PIB), .CLI(CLI), .CRI(CRI),
    .CRE(CRE), .CLE(CLE), .InternalExpression(InternalExpression), .RetCLI(returnexpression_1_retcli),
    .RetCRI(returnexpression_1_retcri), .RetPIB(returnexpression_1_retpib),
    .RetPEB(returnexpression_1_retpeb), .CRI_2(returnexpression_1_cri_2), .CLI_2(returnexpression_1_cli_2),
    .PEB(returnexpression_1_peb), .PIB_2(returnexpression_1_pib_2));
  buf or_14 (or_14_out, returnexpression_1_retpeb);  // OR_Gate
  assign PEB_2 = returnexpression_1_retpeb ? returnexpression_1_peb : 12'bz;  // Controlled_Buffer controlled_buffer_13
  buf or_15 (or_15_out, returnexpression_1_retpib);  // OR_Gate
  assign PIB_2 = returnexpression_1_retpib ? returnexpression_1_pib_2 : 8'bz;  // Controlled_Buffer controlled_buffer_14
  or or_16 (or_16_out, or_11_out, returnexpression_1_retcri);
  assign CRI_2 = returnexpression_1_retcri ? returnexpression_1_cri_2 : 8'bz;  // Controlled_Buffer controlled_buffer_15
  or or_17 (or_17_out, or_12_out, returnexpression_1_retcli);
  assign CLI_2 = returnexpression_1_retcli ? returnexpression_1_cli_2 : 8'bz;  // Controlled_Buffer controlled_buffer_16
  // OR_Gate or_18 has open pins: out=or_18_out
  // OR_Gate or_19 has open pins: out=or_19_out
  // OR_Gate or_20 has open pins: out=or_20_out
  not not_1 (not_1_out, or_14_out);
  assign PEB_2 = not_1_out ? InternalExpression : 12'bz;  // Controlled_Buffer controlled_buffer_17
  not not_2 (not_2_out, or_15_out);
  assign PIB_2 = not_2_out ? {8{1'b0}} : 8'bz;  // Controlled_Buffer controlled_buffer_18
  not not_3 (not_3_out, or_18_out);
  assign CRE_2 = not_3_out ? {12{1'b0}} : 12'bz;  // Controlled_Buffer controlled_buffer_19
  not not_4 (not_4_out, or_16_out);
  assign CRI_2 = not_4_out ? {8{1'b0}} : 8'bz;  // Controlled_Buffer controlled_buffer_20
  not not_5 (not_5_out, or_19_out);
  assign CLE_2 = not_5_out ? {12{1'b0}} : 12'bz;  // Controlled_Buffer controlled_buffer_21
  not not_6 (not_6_out, or_17_out);
  assign CLI_2 = not_6_out ? {8{1'b0}} : 8'bz;  // Controlled_Buffer controlled_buffer_22
  not not_7 (not_7_out, or_13_out);
  assign NewNode_2 = not_7_out ? {12{1'b0}} : 12'bz;  // Controlled_Buffer controlled_buffer_23
  not not_8 (not_8_out, or_20_out);
  assign GeneralOutput = not_8_out ? {8{1'b0}} : 8'bz;  // Controlled_Buffer controlled_buffer_24

  assign EXBWrite = BackStack;
  assign FrontStack = BackStack;
  assign RAMwrite = BackStack;

  // Notes on the sheet:
  //   Input
  //   Output
endmodule

module GoToExpression (
  input  [11:0] PEB,
  input  [7:0] PIB,
  input  [11:0] CRE,
  input  [7:0] CRI,
  input  [11:0] CLE,
  input  [7:0] CLI,
  input  [11:0] InternalExpression,
  output [11:0] PEB_2,
  output [7:0] PIB_2,
  output [11:0] CRE_2,
  output [7:0] CRI_2,
  output [11:0] CLE_2,
  output [7:0] CLI_2
);

  wire decoder_1_out0;

  Decoder #(.select(4)) decoder_1 (
    .out0(decoder_1_out0), .sel(PIB[7:4]));  // open: out1, out2, out3, out4, out5, out6, out7, out8, out9, out10, out11, out12, out13, out14, out15, en
  assign PEB_2 = decoder_1_out0 ? CRE : 12'bz;  // Controlled_Buffer controlled_buffer_1
  assign PIB_2 = decoder_1_out0 ? CRI : 8'bz;  // Controlled_Buffer controlled_buffer_2
  assign CRE_2 = decoder_1_out0 ? PEB : 12'bz;  // Controlled_Buffer controlled_buffer_3
  assign CRI_2 = decoder_1_out0 ? PIB : 8'bz;  // Controlled_Buffer controlled_buffer_4
  assign CLE_2 = decoder_1_out0 ? {12{1'b0}} : 12'bz;  // Controlled_Buffer controlled_buffer_5
  assign CLI_2 = decoder_1_out0 ? {8{1'b0}} : 8'bz;  // Controlled_Buffer controlled_buffer_6

  // Notes on the sheet:
  //   Input
  //   Output
endmodule

module Nullification (
  input  ActivationSignal,
  input  Clock,
  output NullStackClear,
  output NullCLI,
  output NullEXP,
  output NullCRI,
  output [7:0] CRI,
  output [7:0] CLI,
  output [11:0] NewValue
);

  wire d_ff_1_q, not_1_out;

  not not_1 (not_1_out, NullEXP);
  D_Flip_Flop d_ff_1 (.D(NullCLI), .clk(Clock), .Q(d_ff_1_q));  // open: Qn, preset, reset
  and and_1 (NullCLI, ActivationSignal, not_1_out);
  assign CLI = NullCLI ? {8{1'b0}} : 8'bz;  // Controlled_Buffer controlled_buffer_1
  and and_2 (NullEXP, ActivationSignal, d_ff_1_q);
  assign NewValue = NullEXP ? {12{1'b0}} : 12'bz;  // Controlled_Buffer controlled_buffer_2

  assign CRI = CLI;
  assign NullCRI = NullCLI;
  assign NullStackClear = NullEXP;
endmodule

module UpdateExpression (
  input  ActivationSignal,
  input  Clock,
  input  [3:0] UniqueNodeID,
  input  [7:0] PIB,
  input  [11:0] PEB,
  output UpdStackClear,
  output UpdEXP,
  output UpdCLI,
  output UpdCRI,
  output [7:0] CRI,
  output [7:0] CLI,
  output [11:0] NewValue
);

  wire and_2_out, and_3_out, and_5_out, d_ff_1_q, not_1_out;
  wire [3:0] not_2_out, xor_1_out;

  and and_1 (UpdCLI, ActivationSignal, not_1_out);
  not not_1 (not_1_out, and_2_out);
  D_Flip_Flop d_ff_1 (.D(UpdCLI), .clk(Clock), .Q(d_ff_1_q));  // open: Qn, preset, reset
  assign xor_1_out = UniqueNodeID ^ PIB[3:0];  // XOR_Gate xor_1, 4 bits wide
  assign not_2_out = ~xor_1_out;  // NOT_Gate not_2, 4 bits wide
  assign CLI = UpdCLI ? PIB : 8'bz;  // Controlled_Buffer controlled_buffer_1
  and and_2 (and_2_out, ActivationSignal, d_ff_1_q);
  and and_3 (and_3_out, not_2_out[0], not_2_out[1], not_2_out[2], not_2_out[3]);
  and and_4 (UpdEXP, and_3_out, and_2_out);
  and and_5 (and_5_out, and_3_out, and_2_out);
  assign NewValue = and_5_out ? {1'b0, PEB[10:0]} : 12'bz;  // Controlled_Buffer controlled_buffer_2

  assign CRI = CLI;
  assign UpdCRI = UpdCLI;
  assign UpdStackClear = UpdEXP;
endmodule

module UpdatePointerLeft (
  input  ActivationSignal,
  input  Clock,
  input  [3:0] UniqueNodeID,
  input  [7:0] PIB,
  input  [11:0] InternalExpression,
  input  [11:0] PEB,
  output UpdEXP,
  output UpdCLI,
  output UpdCRI,
  output [7:0] CRI,
  output [7:0] CLI,
  output [11:0] NewValue
);

  wire and_2_out, and_3_out, and_5_out, d_ff_1_q, not_1_out;
  wire [3:0] not_2_out, xor_1_out;

  and and_1 (UpdCLI, ActivationSignal, not_1_out);
  not not_1 (not_1_out, and_2_out);
  D_Flip_Flop d_ff_1 (.D(UpdCLI), .clk(Clock), .Q(d_ff_1_q));  // open: Qn, preset, reset
  assign not_2_out = ~xor_1_out;  // NOT_Gate not_2, 4 bits wide
  assign xor_1_out = UniqueNodeID ^ PIB[3:0];  // XOR_Gate xor_1, 4 bits wide
  assign CLI = UpdCLI ? PIB : 8'bz;  // Controlled_Buffer controlled_buffer_1
  and and_2 (and_2_out, ActivationSignal, d_ff_1_q);
  and and_3 (and_3_out, not_2_out[0], not_2_out[1], not_2_out[2], not_2_out[3]);
  and and_4 (UpdEXP, and_3_out, and_2_out);
  and and_5 (and_5_out, and_3_out, and_2_out);
  assign NewValue = and_5_out ? {InternalExpression[11:8], PEB[7:4], InternalExpression[3:0]} : 12'bz;  // Controlled_Buffer controlled_buffer_2

  assign CRI = CLI;
  assign UpdCRI = UpdCLI;
endmodule

module UpdatePointerRight (
  input  ActivationSignal,
  input  Clock,
  input  [3:0] UniqueNodeID,
  input  [7:0] PIB,
  input  [11:0] InternalExpression,
  input  [11:0] PEB,
  output UpdEXP,
  output UpdCLI,
  output UpdCRI,
  output [7:0] CRI,
  output [7:0] CLI,
  output [11:0] NewValue
);

  wire and_2_out, and_3_out, and_5_out, d_ff_1_q, not_1_out;
  wire [3:0] not_2_out, xor_1_out;

  and and_1 (UpdCLI, ActivationSignal, not_1_out);
  not not_1 (not_1_out, and_2_out);
  D_Flip_Flop d_ff_1 (.D(UpdCLI), .clk(Clock), .Q(d_ff_1_q));  // open: Qn, preset, reset
  assign xor_1_out = UniqueNodeID ^ PIB[3:0];  // XOR_Gate xor_1, 4 bits wide
  assign not_2_out = ~xor_1_out;  // NOT_Gate not_2, 4 bits wide
  assign CLI = UpdCLI ? PIB : 8'bz;  // Controlled_Buffer controlled_buffer_1
  and and_2 (and_2_out, ActivationSignal, d_ff_1_q);
  and and_3 (and_3_out, not_2_out[0], not_2_out[1], not_2_out[2], not_2_out[3]);
  and and_4 (UpdEXP, and_3_out, and_2_out);
  and and_5 (and_5_out, and_3_out, and_2_out);
  assign NewValue = and_5_out ? {InternalExpression[11:4], PEB[3:0]} : 12'bz;  // Controlled_Buffer controlled_buffer_2

  assign CRI = CLI;
  assign UpdCRI = UpdCLI;
endmodule

module ReturnExpression (
  input  ActivationSignal,
  input  [3:0] UniqueNodeID,
  input  [7:0] PIB,
  input  [7:0] CLI,
  input  [7:0] CRI,
  input  [11:0] CRE,
  input  [11:0] CLE,
  input  [11:0] InternalExpression,
  output RetPIB,
  output RetCLI,
  output RetPEB,
  output RetCRI,
  output [7:0] CRI_2,
  output [7:0] CLI_2,
  output [11:0] PEB,
  output [7:0] PIB_2
);

  wire and_1_out, and_2_out, and_3_out, and_5_out, and_6_out, and_7_out, or_1_out, or_2_out;
  wire [3:0] not_1_out, not_2_out, not_3_out, xor_1_out, xor_2_out, xor_3_out;

  assign not_1_out = ~xor_1_out;  // NOT_Gate not_1, 4 bits wide
  assign xor_1_out = UniqueNodeID ^ PIB[3:0];  // XOR_Gate xor_1, 4 bits wide
  assign CLI_2 = ActivationSignal ? PIB : 8'bz;  // Controlled_Buffer controlled_buffer_1
  assign xor_2_out = 4'b0011 ^ CLI[7:4];  // XOR_Gate xor_2, 4 bits wide
  assign not_2_out = ~xor_2_out;  // NOT_Gate not_2, 4 bits wide
  assign xor_3_out = 4'b0011 ^ CRI[7:4];  // XOR_Gate xor_3, 4 bits wide
  assign not_3_out = ~xor_3_out;  // NOT_Gate not_3, 4 bits wide
  and and_1 (and_1_out, not_1_out[0], not_1_out[1], not_1_out[2], not_1_out[3]);
  and and_2 (and_2_out, not_2_out[0], not_2_out[1], not_2_out[2], not_2_out[3]);
  and and_3 (and_3_out, not_3_out[0], not_3_out[1], not_3_out[2], not_3_out[3]);
  and and_4 (RetPEB, or_1_out, ActivationSignal);
  or or_1 (or_1_out, and_1_out, and_2_out, and_3_out);
  and and_5 (and_5_out, and_1_out, ActivationSignal);
  and and_6 (and_6_out, and_2_out, ActivationSignal);
  and and_7 (and_7_out, and_3_out, ActivationSignal);
  assign PEB = and_6_out ? CLE : 12'bz;  // Controlled_Buffer controlled_buffer_2
  assign PEB = and_5_out ? InternalExpression : 12'bz;  // Controlled_Buffer controlled_buffer_3
  assign PEB = and_7_out ? CRE : 12'bz;  // Controlled_Buffer controlled_buffer_4
  or or_2 (or_2_out, and_5_out, and_6_out, and_7_out);
  assign PIB_2 = or_2_out ? 8'h30 : 8'bz;  // Controlled_Buffer controlled_buffer_5

  assign CRI_2 = CLI_2;
  assign RetCLI = ActivationSignal;
  assign RetCRI = ActivationSignal;
  assign RetPIB = RetPEB;

  // Notes on the sheet:
  //   Marker Signal is 0011
  //   Marker Signal is 0011
endmodule

module BranchChop (
  input  Clock,
  input  [7:0] CLI,
  input  [7:0] CRI,
  input  [11:0] InternalExpression,
  output BraNew,
  output [11:0] NewValue
);

  wire and_1_out, and_2_out, or_1_out;
  wire [3:0] not_1_out, not_2_out, xor_1_out, xor_2_out;

  assign xor_1_out = CLI[7:4] ^ 4'b0001;  // XOR_Gate xor_1, 4 bits wide
  assign xor_2_out = CRI[7:4] ^ 4'b0001;  // XOR_Gate xor_2, 4 bits wide
  assign not_1_out = ~xor_1_out;  // NOT_Gate not_1, 4 bits wide
  assign not_2_out = ~xor_2_out;  // NOT_Gate not_2, 4 bits wide
  D_Flip_Flop d_ff_1 (.D(or_1_out), .clk(Clock), .Q(BraNew));  // open: Qn, preset, reset
  or or_1 (or_1_out, and_2_out, and_1_out);
  and and_1 (and_1_out, not_1_out[0], not_1_out[1], not_1_out[2], not_1_out[3]);
  and and_2 (and_2_out, not_2_out[0], not_2_out[1], not_2_out[2], not_2_out[3]);
  assign NewValue = and_2_out ? {4'b0000, InternalExpression[7:4], 3'b100, InternalExpression[0]} : 12'bz;  // Controlled_Buffer controlled_buffer_1
  assign NewValue = and_1_out ? {4'b0000, InternalExpression[11:8], 3'b100, InternalExpression[0]} : 12'bz;  // Controlled_Buffer controlled_buffer_2
endmodule

module CompareValue (
  input  ActivationSignal,
  input  Clock,
  input  Clear,
  input  [11:0] InternalValue,
  input  [11:0] PEB,
  input  [7:0] PIB,
  input  [7:0] CRI,
  input  [7:0] CLI,
  output MarkForTransformation,
  output [7:0] CLI_2,
  output [7:0] CRI_2,
  output [7:0] PIB_2
);

  wire and_1_out, and_2_out, and_3_out, and_4_out, and_5_out, controlled_buffer_5_out, not_5_out;
  wire [2:0] not_1_out, xor_1_out;
  wire [3:0] not_2_out, not_4_out, xor_2_out, xor_4_out;
  wire [7:0] controlled_buffer_1_out, not_3_out, xor_3_out;

  assign not_1_out = ~xor_1_out;  // NOT_Gate not_1, 3 bits wide
  assign xor_1_out = 3'b010 ^ InternalValue[10:8];  // XOR_Gate xor_1, 3 bits wide
  assign not_2_out = ~xor_2_out;  // NOT_Gate not_2, 4 bits wide
  assign xor_2_out = 4'b0100 ^ CRI[7:4];  // XOR_Gate xor_2, 4 bits wide
  and and_1 (and_1_out, not_1_out[0], not_1_out[1], not_1_out[2]);
  assign xor_3_out = InternalValue[7:0] ^ PEB[7:0];  // XOR_Gate xor_3, 8 bits wide
  assign not_3_out = ~xor_3_out;  // NOT_Gate not_3, 8 bits wide
  and and_2 (and_2_out, not_2_out[0], not_2_out[1], not_2_out[2], not_2_out[3]);
  and and_3 (and_3_out, not_3_out[0], not_3_out[1], not_3_out[2], not_3_out[3], not_3_out[4], not_3_out[5], not_3_out[6], not_3_out[7]);
  assign controlled_buffer_1_out = and_2_out ? CRI : 8'bz;  // Controlled_Buffer controlled_buffer_1
  assign xor_4_out = 4'b0100 ^ CLI[7:4];  // XOR_Gate xor_4, 4 bits wide
  assign not_4_out = ~xor_4_out;  // NOT_Gate not_4, 4 bits wide
  assign controlled_buffer_1_out = and_4_out ? CLI : 8'bz;  // Controlled_Buffer controlled_buffer_2
  and and_4 (and_4_out, not_4_out[0], not_4_out[1], not_4_out[2], not_4_out[3]);
  not not_5 (not_5_out, and_1_out);
  assign CLI_2 = and_1_out ? PIB : 8'bz;  // Controlled_Buffer controlled_buffer_3
  assign PIB_2 = and_1_out ? controlled_buffer_1_out : 8'bz;  // Controlled_Buffer controlled_buffer_4
  and and_5 (and_5_out, ActivationSignal, controlled_buffer_5_out);
  assign controlled_buffer_5_out = not_5_out ? and_3_out : 1'bz;  // Controlled_Buffer controlled_buffer_5
  assign PIB_2 = not_5_out ? 8'h40 : 8'bz;  // Controlled_Buffer controlled_buffer_6
  D_Flip_Flop d_ff_1 (.D(and_5_out), .clk(Clock), .Q(MarkForTransformation), .reset(Clear));  // open: Qn, preset

  assign CRI_2 = CLI_2;
endmodule

module ImmediateResolution (
  input  ActivationSignal,
  output ImmPIB,
  output [7:0] PIB
);

  assign PIB = ActivationSignal ? 8'h10 : 8'bz;  // Controlled_Buffer controlled_buffer_1

  assign ImmPIB = ActivationSignal;
endmodule

module PrepareForTransformationAsAncestorInput (
  input  ActivationSignal,
  input  Clock,
  input  [3:0] SFS,
  input  [3:0] SBS,
  input  [3:0] RAM,
  input  [3:0] UniqueNodeID,
  input  [7:0] CLI,
  input  [7:0] CRI,
  input  [11:0] CLE,
  input  [11:0] CRE,
  input  [11:0] InternalExpression,
  output ptaSEL,
  output ptaRAM,
  output ptaSFS,
  output ptaPIB,
  output ptaSBS,
  output ptaStackClear,
  output [7:0] GeneralOuput,
  output [11:0] PEB,
  output [7:0] CLI_2,
  output [7:0] CLE_2
);

  wire and_1_out, and_2_out, and_3_out, and_4_out, and_5_out, and_6_out, and_7_out, and_8_out, and_9_out,
       and_10_out, and_11_out, and_12_out, and_13_out, and_14_out, and_15_out, and_16_out, and_17_out,
       and_18_out, and_19_out, and_20_out, and_21_out, and_22_out, and_23_out, and_25_out, and_27_out,
       d_ff_1_q, d_ff_2_q, d_ff_3_q, d_ff_4_q, d_ff_5_q, d_ff_6_q, d_ff_7_q, d_ff_8_q, d_ff_9_q, d_ff_10_q,
       not_1_out, not_9_out, not_10_out, or_1_out, or_4_out, or_5_out, or_7_out, or_8_out, or_9_out,
       or_11_out, or_12_out, or_13_out, or_14_out, or_15_out, or_16_out, or_17_out, or_18_out, or_19_out,
       or_20_out, or_21_out, or_22_out, or_23_out, or_24_out, or_25_out;
  wire [2:0] not_7_out, not_8_out, xor_6_out, xor_7_out;
  wire [3:0] adder_1_out, adder_2_out, not_2_out, not_3_out, not_4_out, not_5_out, not_6_out, xor_1_out,
       xor_2_out, xor_3_out, xor_4_out, xor_5_out;
  wire [11:0] controlled_buffer_2_out, register_1_q;

  not not_1 (not_1_out, or_1_out);
  assign xor_1_out = 4'b0000 ^ SFS;  // XOR_Gate xor_1, 4 bits wide
  assign xor_2_out = 4'b0011 ^ CLI[7:4];  // XOR_Gate xor_2, 4 bits wide
  assign xor_3_out = 4'b0011 ^ CRI[7:4];  // XOR_Gate xor_3, 4 bits wide
  D_Flip_Flop d_ff_1 (.D(and_1_out), .clk(Clock), .Q(d_ff_1_q));  // open: Qn, preset, reset
  and and_1 (and_1_out, ActivationSignal, not_1_out);
  assign not_2_out = ~xor_1_out;  // NOT_Gate not_2, 4 bits wide
  assign not_3_out = ~xor_4_out;  // NOT_Gate not_3, 4 bits wide
  assign xor_4_out = RAM ^ UniqueNodeID;  // XOR_Gate xor_4, 4 bits wide
  Adder #(.width(4)) adder_1 (.a(4'b0001), .b(SFS), .out(adder_1_out));  // open: cin, cout
  Adder #(.width(4)) adder_2 (.a(4'b0001), .b(SBS), .out(adder_2_out));  // open: cin, cout
  assign xor_5_out = SFS ^ SBS;  // XOR_Gate xor_5, 4 bits wide
  assign not_4_out = ~xor_5_out;  // NOT_Gate not_4, 4 bits wide
  assign not_5_out = ~xor_2_out;  // NOT_Gate not_5, 4 bits wide
  assign not_6_out = ~xor_3_out;  // NOT_Gate not_6, 4 bits wide
  and and_2 (and_2_out, and_3_out, and_4_out);
  or or_1 (or_1_out, and_3_out, or_4_out);
  and and_3 (and_3_out, ActivationSignal, d_ff_1_q);
  and and_4 (and_4_out, not_2_out[0], not_2_out[1], not_2_out[2], not_2_out[3]);
  and and_5 (and_5_out, and_3_out, and_4_out);
  and and_6 (and_6_out, not_3_out[0], not_3_out[1], not_3_out[2], not_3_out[3]);
  and and_7 (and_7_out, not_4_out[0], not_4_out[1], not_4_out[2], not_4_out[3]);
  and and_8 (and_8_out, not_5_out[0], not_5_out[1], not_5_out[2], not_5_out[3]);
  and and_9 (and_9_out, not_6_out[0], not_6_out[1], not_6_out[2], not_6_out[3]);
  or or_2 (ptaRAM, and_2_out, or_13_out);
  D_Flip_Flop d_ff_2 (.D(and_3_out), .clk(Clock), .Q(d_ff_2_q));  // open: Qn, preset, reset
  assign GeneralOuput = and_5_out ? {4'b0000, UniqueNodeID} : 8'bz;  // Controlled_Buffer controlled_buffer_1
  assign controlled_buffer_2_out = and_8_out ? CLE : 12'bz;  // Controlled_Buffer controlled_buffer_2
  assign controlled_buffer_2_out = and_9_out ? CRE : 12'bz;  // Controlled_Buffer controlled_buffer_3
  assign controlled_buffer_2_out = and_6_out ? InternalExpression : 12'bz;  // Controlled_Buffer controlled_buffer_4
  or or_3 (ptaSFS, and_10_out, or_8_out);
  and and_10 (and_10_out, and_11_out, and_4_out);
  or or_4 (or_4_out, and_11_out, or_5_out);
  and and_11 (and_11_out, ActivationSignal, d_ff_2_q);
  and and_12 (and_12_out, and_11_out, and_4_out);
  assign GeneralOuput = and_12_out ? {4'b0000, adder_1_out} : 8'bz;  // Controlled_Buffer controlled_buffer_5
  or or_5 (or_5_out, and_13_out, or_9_out);
  D_Flip_Flop d_ff_3 (.D(and_11_out), .clk(Clock), .Q(d_ff_3_q));  // open: Qn, preset, reset
  or or_6 (ptaPIB, and_13_out, or_7_out);
  and and_13 (and_13_out, ActivationSignal, d_ff_3_q);
  Register #(.width(12)) register_1 (
    .D(controlled_buffer_2_out), .en(1'b1), .clk(and_13_out), .Q(register_1_q), .clr(and_1_out));
  assign PEB = and_13_out ? controlled_buffer_2_out : 12'bz;  // Controlled_Buffer controlled_buffer_6
  assign CLI_2 = and_13_out ? {4'b0101, RAM} : 8'bz;  // Controlled_Buffer controlled_buffer_7
  assign CLE_2 = and_13_out ? {4'b0101, RAM} : 8'bz;  // Controlled_Buffer controlled_buffer_8
  or or_7 (or_7_out, or_12_out, and_15_out);
  or or_8 (or_8_out, and_20_out, and_14_out);
  or or_9 (or_9_out, and_15_out, or_15_out);
  D_Flip_Flop d_ff_4 (.D(and_13_out), .clk(Clock), .Q(d_ff_4_q));  // open: Qn, preset, reset
  assign xor_6_out = 3'b101 ^ register_1_q[10:8];  // XOR_Gate xor_6, 3 bits wide
  assign not_7_out = ~xor_6_out;  // NOT_Gate not_7, 3 bits wide
  assign not_8_out = ~xor_7_out;  // NOT_Gate not_8, 3 bits wide
  assign xor_7_out = 3'b001 ^ register_1_q[10:8];  // XOR_Gate xor_7, 3 bits wide
  or or_10 (ptaSEL, and_15_out, or_11_out);
  and and_14 (and_14_out, and_15_out, or_14_out);
  and and_15 (and_15_out, ActivationSignal, d_ff_4_q);
  assign GeneralOuput = and_15_out ? {4'b0000, adder_1_out} : 8'bz;  // Controlled_Buffer controlled_buffer_9
  assign PEB = and_15_out ? register_1_q : 12'bz;  // Controlled_Buffer controlled_buffer_10
  not not_9 (not_9_out, and_16_out);
  and and_16 (and_16_out, not_7_out[0], not_7_out[1], not_7_out[2]);
  and and_17 (and_17_out, not_8_out[0], not_8_out[1], not_8_out[2]);
  or or_11 (or_11_out, or_19_out, and_19_out);
  or or_12 (or_12_out, or_20_out, and_19_out);
  or or_13 (or_13_out, and_22_out, and_18_out);
  and and_18 (and_18_out, or_14_out, and_19_out);
  D_Flip_Flop d_ff_5 (.D(and_15_out), .clk(Clock), .Q(d_ff_5_q));  // open: Qn, preset, reset
  or or_14 (or_14_out, not_9_out, not_10_out);
  or or_15 (or_15_out, and_19_out, or_17_out);
  and and_19 (and_19_out, ActivationSignal, d_ff_5_q);
  or or_16 (or_16_out, and_19_out, or_18_out);
  assign PEB = or_16_out ? register_1_q : 12'bz;  // Controlled_Buffer controlled_buffer_11
  or or_17 (or_17_out, and_21_out, or_22_out);
  D_Flip_Flop d_ff_6 (.D(and_19_out), .clk(Clock), .Q(d_ff_6_q));  // open: Qn, preset, reset
  or or_18 (or_18_out, and_21_out, or_23_out);
  assign GeneralOuput = and_18_out ? {4'b0000, register_1_q[7:4]} : 8'bz;  // Controlled_Buffer controlled_buffer_12
  or or_19 (or_19_out, and_22_out, and_20_out);
  or or_20 (or_20_out, or_21_out, and_20_out);
  and and_20 (and_20_out, not_10_out, and_21_out);
  and and_21 (and_21_out, ActivationSignal, d_ff_6_q);
  not not_10 (not_10_out, and_17_out);
  D_Flip_Flop d_ff_7 (.D(and_21_out), .clk(Clock), .Q(d_ff_7_q));  // open: Qn, preset, reset
  assign GeneralOuput = and_20_out ? {4'b0000, adder_1_out} : 8'bz;  // Controlled_Buffer controlled_buffer_13
  or or_21 (or_21_out, or_24_out, and_22_out);
  and and_22 (and_22_out, not_10_out, and_23_out);
  buf or_22 (or_22_out, and_23_out);  // OR_Gate
  and and_23 (and_23_out, ActivationSignal, d_ff_7_q);
  or or_23 (or_23_out, and_23_out, or_25_out);
  assign GeneralOuput = and_23_out ? {4'b0000, register_1_q[3:0]} : 8'bz;  // Controlled_Buffer controlled_buffer_14
  or or_24 (or_24_out, ptaStackClear, ptaSBS);
  D_Flip_Flop d_ff_8 (.D(and_23_out), .clk(Clock), .Q(d_ff_8_q));  // open: Qn, preset, reset
  or or_25 (or_25_out, ptaSBS, and_27_out);
  D_Flip_Flop d_ff_9 (.D(ptaSBS), .clk(Clock), .Q(d_ff_9_q));  // open: Qn, preset, reset
  and and_24 (ptaSBS, ActivationSignal, d_ff_8_q);
  assign GeneralOuput = ptaSBS ? {4'b0000, adder_2_out} : 8'bz;  // Controlled_Buffer controlled_buffer_15
  D_Flip_Flop d_ff_10 (.D(and_25_out), .clk(Clock), .Q(d_ff_10_q));  // open: Qn, preset, reset
  and and_25 (and_25_out, ActivationSignal, d_ff_9_q);
  and and_26 (ptaStackClear, and_27_out, and_7_out);
  and and_27 (and_27_out, ActivationSignal, d_ff_10_q);

  // Notes on the sheet:
  //   New SFS
  //   New SBS
  //   RAM on == Write
  //   off == Read
  //   SEL off == SBS
  //   on == SFS
endmodule
